// Logisim project control-logic.circ as structural Verilog: 1 circuit, main circuit control_logic
module control_logic (
  input  [31:0] Instruction,
  input  BrEq,
  input  BrLt,
  output PCSel,
  output RegWEn,
  output [2:0] ImmSel,
  output BrUn,
  output ASel,
  output BSel,
  output [3:0] ALUSel,
  output MemWEn,
  output [1:0] WBSel
);

  wire B, I, IL, jal, jalr, or_1_out, s, U, undriven, WEn1, WEn2, WEn3, WEn4, WEn5, WEn6, WEn7, WEn8, WEn9,
       WEn10, WEn11, WEn12, WEn13, WEn14, WEn15;
  wire [15:0] rom_1_data;

  ROM #(.addrWidth(6), .dataWidth(16)) rom_1 (.data(rom_1_data));  // open: addr
  or or_1 (or_1_out, I, jalr, IL);
  Priority_Encoder priority_encoder_1 (
    .in0(or_1_out), .in1(s), .in2(B), .in3(U), .in4(jal), .out(ImmSel));  // open: in5, in6, in7, en_in, gs, en_out
  Priority_Encoder #(.select_enc(4)) priority_encoder_2 (
    .in0(undriven), .in1(WEn1), .in2(WEn2), .in3(WEn3), .in4(WEn4), .in5(WEn5), .in6(WEn6), .in7(WEn7),
    .in8(WEn8), .in9(WEn9), .in10(WEn10), .in11(WEn11), .in12(WEn12), .in13(WEn13), .in14(WEn14), .in15(WEn15));  // open: out, gs, en_out, en_in

  // Other names for the same wires on the sheet: opcode[6:0] = Instruction[6:0]; rd[4:0] = Instruction[11:7];
  //   funct3[2:0] = Instruction[14:12]; rs1[4:0] = Instruction[19:15]; rs2[4:0] = Instruction[24:20];
  //   funct7[6:0] = Instruction[31:25]

  // Notes on the sheet:
  //   INPUTS to your circuit
  //   Connect ROM Input here ->
  //   ROM FOR CONTROL LOGIC
  //   DON'T CHANGE THE LOCATIONS OF THE INPUTS AND OUTPUTS!
  //   This is only if you choose to do the ROM option
  //   CONNECT
  //   WIRE
  //   TO
  //   USE
  //   ROM
  //   OUTPUT from your circuit
  //   Reminder: If using ROM, use combinational logic for PCSel
endmodule
