// Logisim project cpu.circ as structural Verilog: 1 circuit, main circuit cpu
module cpu (
  input  clk,
  input  [31:0] Instruction,
  input  [31:0] MemReadData,
  output [31:0] MemAddress,
  output [31:0] ProgramCounter,
  output [31:0] ra,
  output [31:0] sp,
  output [31:0] t0,
  output [31:0] t1,
  output [31:0] t2,
  output [31:0] s0,
  output [31:0] s1,
  output [31:0] a0,
  output [3:0] MemWriteMask,
  output [31:0] MemWriteData
);

  wire branch_comp_1_p4, branch_comp_1_p5, control_logic_1_asel, control_logic_1_brun, control_logic_1_bsel,
       control_logic_1_memwen, control_logic_1_pcsel, control_logic_1_regwen, partial_store_1_p5,
       partial_store_1_p6, partial_store_1_p8, partial_store_1_p10;
  wire [1:0] control_logic_1_wbsel;
  wire [2:0] control_logic_1_immsel;
  wire [3:0] control_logic_1_alusel;
  wire [31:0] adder_1_out, adder_2_out, ALUR1, imm_gen_1_immediate, Memory, multiplexer_1_out,
       multiplexer_2_out, multiplexer_3_out, regfile_1_regreaddata1, regfile_1_regreaddata2, WriteR;

  Adder #(.width(32)) adder_1 (.a(ProgramCounter), .b(32'h4), .out(adder_1_out));  // open: cin, cout
  Register #(.width(32)) register_1 (.D(MemAddress), .clk(clk), .Q(ALUR1));  // open: en, clr
  Register #(.width(32)) PC (.D(multiplexer_1_out), .clk(clk), .Q(ProgramCounter));  // open: en, clr
  Multiplexer #(.width(32)) multiplexer_1 (
    .in0(adder_1_out), .in1(MemAddress), .out(multiplexer_1_out), .sel(control_logic_1_pcsel));
  control_logic control_logic_1 (
    .PCSel(control_logic_1_pcsel), .RegWEn(control_logic_1_regwen), .ImmSel(control_logic_1_immsel),
    .BrUn(control_logic_1_brun), .ASel(control_logic_1_asel), .BSel(control_logic_1_bsel),
    .ALUSel(control_logic_1_alusel), .MemWEn(control_logic_1_memwen), .WBSel(control_logic_1_wbsel),
    .Instruction(Instruction), .BrEq(branch_comp_1_p4), .BrLt(branch_comp_1_p5));
  regfile regfile_1 (
    .ReadReg1(Instruction[19:15]), .ReadReg2(Instruction[24:20]), .WriteReg(Instruction[11:7]),
    .RegWriteData(WriteR), .RegWEn(control_logic_1_regwen), .clk(clk), .ra(ra), .sp(sp), .t0(t0), .t1(t1),
    .t2(t2), .s0(s0), .s1(s1), .a0(a0), .RegReadData1(regfile_1_regreaddata1),
    .RegReadData2(regfile_1_regreaddata2));
  imm_gen imm_gen_1 (.Instruction(Instruction), .ImmSel(control_logic_1_immsel), .Immediate(imm_gen_1_immediate));
  // branch_comp branch_comp_1: pin names not known; wires that end beside it: regfile_1_regreaddata1, regfile_1_regreaddata2, control_logic_1_brun, branch_comp_1_p4, branch_comp_1_p5
  Multiplexer #(.width(32)) multiplexer_2 (
    .in0(regfile_1_regreaddata1), .in1(ProgramCounter), .out(multiplexer_2_out), .sel(control_logic_1_asel));
  Multiplexer #(.width(32)) multiplexer_3 (
    .in0(regfile_1_regreaddata2), .in1(imm_gen_1_immediate), .out(multiplexer_3_out),
    .sel(control_logic_1_bsel));
  alu alu_1 (.ALUResult(MemAddress), .A(multiplexer_2_out), .B(multiplexer_3_out), .ALUSel(control_logic_1_alusel));
  Adder #(.width(32)) adder_2 (.a(ProgramCounter), .b(32'h4), .out(adder_2_out));  // open: cin, cout
  Multiplexer #(.select(2), .width(32)) multiplexer_4 (
    .in0(Memory), .in1(MemAddress), .in2(adder_2_out), .out(WriteR), .sel(control_logic_1_wbsel));  // open: in3
  // partial_store partial_store_1: pin names not known; wires that end beside it: Instruction, MemAddress, regfile_1_regreaddata2, control_logic_1_memwen, partial_store_1_p5, partial_store_1_p6, partial_store_1_p6, partial_store_1_p8, partial_store_1_p8, partial_store_1_p10, MemWriteMask, MemWriteData, partial_store_1_p5, partial_store_1_p10
  // partial_load partial_load_1: pin names not known; wires that end beside it: Instruction, MemAddress, MemWriteData, Memory

  // Other names for the same wires on the sheet: ALUR[31:0] = MemAddress

  // Notes on the sheet:
  //   To IMEM
  //   IMEM (do **NOT** move this)
  //   From IMEM
  //   Inputs/Outputs for testing. Do **NOT** move these.
  //   It is OK to move the PC, RegFile, ALU, MEM, Branch Comp, Imm Gen, Partial Load, Partial Store and Control Logic to wherever is most convenient for you when constructing your CPU, and to delete this text
  //   To DMEM
  //   DMEM (do **NOT** move this)
  //   From DMEM
endmodule
